# Fritzing sketch weather sensor (saved by Fritzing 0.8.7b)

parts:
  Compass = Triple Axis Magnetometer - HMC5883 Breakout
  Pro_Mini_3_3v_8MHz = Arduino Pro Mini v13
  RTC = Real Time Clock Module - DS1307 RTC Breakout Board [part_number=DS3231]
  SD_Card_Reader = SD Card Break out
  Weather_Sensor = mystery part, 3 pins [chip_label=?]
  LED1 = LED - 5mm [color="Green (565nm)" package="5 mm [THT]"]
  LED2 = LED - 5mm [color="Red (633nm)" package="5 mm [THT]"]
  R1 = Resistor [tolerance=±5% resistance=220 package=THT]

nets:
  GND: Compass.GND, Pro_Mini_3_3v_8MHz.GND, RTC.GND, SD_Card_Reader.GND
  VCC: Compass.VCC, Pro_Mini_3_3v_8MHz.VCC
  N1: Compass.SDA, Pro_Mini_3_3v_8MHz.A4, RTC.SDA
  N2: Compass.SCL, Pro_Mini_3_3v_8MHz.A5, RTC.SCL
  N3: Pro_Mini_3_3v_8MHz.A0, Weather_Sensor.pin2
  N4: Pro_Mini_3_3v_8MHz.D13/SCK, SD_Card_Reader.CLK
  N5: Pro_Mini_3_3v_8MHz.D12/MISO, SD_Card_Reader.DI
  N6: Pro_Mini_3_3v_8MHz.D11_PWM/MOSI, SD_Card_Reader.DO
  N7: Pro_Mini_3_3v_8MHz.D10_PWM/SS, SD_Card_Reader.CS
  N8: Pro_Mini_3_3v_8MHz.D6_PWM, LED1.anode, LED2.cathode
  N9: Pro_Mini_3_3v_8MHz.D5_PWM, R1.Pin_1
  N10: Pro_Mini_3_3v_8MHz.D4, RTC.5V
  N11: Pro_Mini_3_3v_8MHz.D3_PWM, Weather_Sensor.pin1
  N12: Pro_Mini_3_3v_8MHz.D2, RTC.SQW
  N13: LED1.cathode, LED2.anode, R1.Pin_0

notes:
  Notes:
  Cut trace to voltage regulator on Pro Mini
  Cut voltage regulator off of SD break out board
  Anemometer output to D3 (interrupt 2)
  Weather vane output to A0

custom parts:
  SD Card Break out: ADA Fruit part #ID: 254
